# Fritzing sketch adding-power-button-to-raspberry-pi (saved by Fritzing 0.9.5d)
breadboards: 1

parts:
  MCU1 = Raspberry Pi Zero
  S1 = Pushbutton [package="[THT]"]

nets:
  N1: MCU1.pin_5, S1.Pin_1, S1.Pin_2
  N2: MCU1.pin_9, MCU1.pin_39, S1.Pin_3, S1.Pin_4
