# Fritzing sketch blinking-led-on-raspberry-pi (saved by Fritzing 0.9.5d)
breadboards: 1

parts:
  MCU1 = Raspberry Pi Zero
  LED1 = LED - 5mm [color="Red (633nm)" package="5 mm [THT]"]
  R1 = Resistor [tolerance=±5% resistance=1k package=THT]

nets:
  N1: MCU1.pin_7, R1.Pin_1
  N2: MCU1.pin_9, LED1.cathode
  N3: LED1.anode, R1.Pin_0
