# Fritzing sketch power-through-gpio-pins (saved by Fritzing 0.9.5d)
breadboards: 1

parts:
  MCU1 = Raspberry Pi Zero
  J1 = micro USB connector MK5P [package=usb-microb]

nets:
  N1: MCU1.pin_2, MCU1.pin_4, J1.VCC
  N2: MCU1.pin_6, J1.GND

custom parts:
  micro USB connector MK5P: micro USB connector which only uses holes no slots. Apparently a standard of some kind called MK5P. Note the text in pcb that marks the edge of the board (and the amount the connector protudes) will both be truncated from the final board if aligned correctly.
