# Fritzing sketch turn-on-led-with-pir-sensor (saved by Fritzing 0.9.5d)
breadboards: 1

parts:
  MCU1 = Raspberry Pi Zero
  LED1 = LED - 5mm [color="Red (633nm)" package="5 mm [THT]"]
  R1 = Resistor [tolerance=±5% resistance=1k package=THT]
  パーツ1 = HC-SR501 Body Sensor Module

nets:
  N1: MCU1.pin_2, MCU1.pin_4, パーツ1.VCC
  N2: MCU1.pin_6, MCU1.pin_9, MCU1.pin_25, LED1.cathode, パーツ1.GND
  N3: MCU1.pin_13, パーツ1.OUT
  N4: MCU1.pin_15, R1.Pin_1
  N5: LED1.anode, R1.Pin_0

custom parts:
  HC-SR501 Body Sensor Module: Pyroelectric Infrared PIR Motion Sensor Detector Module
